# Fritzing sketch timer (saved by Fritzing 0.9.3b)
breadboards: 1

parts:
  Part1 = Arduino Uno (Rev3)
  7_Segment1 = 7 Segment Display
  R1 = Resistor [tolerance=±5% resistance=220 package=THT]
  R2 = Resistor [tolerance=±5% resistance=220 package=THT]
  R3 = Resistor [tolerance=±5% resistance=220 package=THT]
  R4 = Resistor [tolerance=±5% resistance=220 package=THT]
  R5 = Resistor [tolerance=±5% resistance=220 package=THT]
  R6 = Resistor [tolerance=±5% resistance=220 package=THT]
  R7 = Resistor [tolerance=±5% resistance=220 package=THT]

nets:
  N1: Part1.D8, R5.Pin_0
  N2: Part1.D10_PWM/SS, R6.Pin_0
  N3: Part1.D12/MISO, R7.Pin_0
  N4: Part1.D2, R4.Pin_1
  N5: Part1.D4, R3.Pin_1
  N6: Part1.D6_PWM, R2.Pin_1
  N7: Part1.D7, R1.Pin_1
  N8: Part1.5V, 7_Segment1.Segment_G
  N9: 7_Segment1.Segment_F, R4.Pin_0
  N10: 7_Segment1.common_anode, R3.Pin_0, R7.Pin_1
  N11: 7_Segment1.Segment_E, R2.Pin_0
  N12: 7_Segment1.Segment_D, R1.Pin_0
  N13: 7_Segment1.Segment_B, R6.Pin_1
  N14: 7_Segment1.Segment_A, R5.Pin_1
